// Logisim project CPU_DESIGN.circ as structural Verilog
module one_bit_memory (
  input  i,
  input  s,
  output o
);

  wire nand_1_out, nand_2_out, nand_4_out;

  nand nand_1 (nand_1_out, i, s);
  nand nand_2 (nand_2_out, nand_1_out, s);
  nand nand_3 (o, nand_1_out, nand_4_out);
  nand nand_4 (nand_4_out, o, nand_2_out);
endmodule

module eight_bit_memory (
  input  s,
  input  [7:0] i,
  output [7:0] o
);

  one_bit_memory one_bit_memory_1 (.i(i[0]), .s(s), .o(o[0]));
  one_bit_memory one_bit_memory_2 (.i(i[1]), .s(s), .o(o[1]));
  one_bit_memory one_bit_memory_3 (.i(i[2]), .s(s), .o(o[2]));
  one_bit_memory one_bit_memory_4 (.i(i[3]), .s(s), .o(o[3]));
  one_bit_memory one_bit_memory_5 (.i(i[4]), .s(s), .o(o[4]));
  one_bit_memory one_bit_memory_6 (.i(i[5]), .s(s), .o(o[5]));
  one_bit_memory one_bit_memory_7 (.i(i[6]), .s(s), .o(o[6]));
  one_bit_memory one_bit_memory_8 (.i(i[7]), .s(s), .o(o[7]));
endmodule

module eight_bit_register (
  input  e,
  input  s,
  input  [7:0] i,
  output [7:0] o
);

  wire [7:0] controlled_buffer_1_out, eight_bit_memory_1_o, enabler_1_o;

  assign controlled_buffer_1_out = s ? i : 8'bz;  // Controlled_Buffer controlled_buffer_1
  eight_bit_memory eight_bit_memory_1 (.s(s), .i(controlled_buffer_1_out), .o(eight_bit_memory_1_o));
  enabler enabler_1 (.e(e), .i(eight_bit_memory_1_o), .o(enabler_1_o));
  assign o = e ? enabler_1_o : 8'bz;  // Controlled_Buffer controlled_buffer_2
endmodule

module enabler (
  input  e,
  input  [7:0] i,
  output [7:0] o
);

  and and_1 (o[0], e, i[0]);
  and and_2 (o[1], e, i[1]);
  and and_3 (o[2], e, i[2]);
  and and_4 (o[3], e, i[3]);
  and and_5 (o[4], e, i[4]);
  and and_6 (o[5], e, i[5]);
  and and_7 (o[6], e, i[6]);
  and and_8 (o[7], e, i[7]);
endmodule

module enabler_ver2 (
  input  [7:0] i,
  input  e,
  output [7:0] o
);

  assign o = e ? i : 8'bz;  // Controlled_Buffer controlled_buffer_1
endmodule

module one_byte_ram (
  input  y,
  input  x,
  input  bus_set,
  input  bus_enable,
  input  [7:0] bus_input,
  output [7:0] bus_output
);

  wire and_1_out, and_2_out, and_3_out;
  wire [7:0] controlled_buffer_1_out, eight_bit_register_1_o;

  and and_1 (and_1_out, y, x);
  assign controlled_buffer_1_out = and_1_out ? bus_input : 8'bz;  // Controlled_Buffer controlled_buffer_1
  and and_2 (and_2_out, and_1_out, bus_set);
  and and_3 (and_3_out, and_1_out, bus_enable);
  eight_bit_register eight_bit_register_1 (
    .e(and_2_out), .s(and_3_out), .i(controlled_buffer_1_out), .o(eight_bit_register_1_o));
  assign bus_output = and_1_out ? eight_bit_register_1_o : 8'bz;  // Controlled_Buffer controlled_buffer_2
endmodule

module ram_256_byte (
  input  set_address,
  input  [7:0] address,
  input  [7:0] bus_input,
  input  bus_set,
  input  bus_enable,
  output [7:0] out_6
);

  wire decoder_1_out0, decoder_1_out1, decoder_1_out2, decoder_1_out3, decoder_1_out4, decoder_1_out5,
       decoder_1_out6, decoder_1_out7, decoder_1_out8, decoder_1_out9, decoder_1_out11, decoder_1_out12,
       decoder_1_out13, decoder_1_out14, decoder_1_out15, decoder_2_out0, decoder_2_out1, decoder_2_out2,
       decoder_2_out3, decoder_2_out4, decoder_2_out5, decoder_2_out6, decoder_2_out7, decoder_2_out8,
       decoder_2_out9, decoder_2_out10, decoder_2_out11, decoder_2_out12, decoder_2_out13, decoder_2_out14,
       decoder_2_out15;
  wire [7:0] controlled_buffer_1_out, eight_bit_register_1_o;

  eight_bit_register eight_bit_register_1 (.e(1'b1), .s(set_address), .i(address), .o(eight_bit_register_1_o));
  Decoder #(.enable("false"), .select(4)) decoder_1 (
    .out0(decoder_1_out0), .out1(decoder_1_out1), .out2(decoder_1_out2), .out3(decoder_1_out3),
    .out4(decoder_1_out4), .out5(decoder_1_out5), .out6(decoder_1_out6), .out7(decoder_1_out7),
    .out8(decoder_1_out8), .out9(decoder_1_out9), .out10(decoder_1_out8), .out11(decoder_1_out11),
    .out12(decoder_1_out12), .out13(decoder_1_out13), .out14(decoder_1_out14), .out15(decoder_1_out15),
    .sel(eight_bit_register_1_o[7:4]));
  assign controlled_buffer_1_out = bus_set ? bus_input : 8'bz;  // Controlled_Buffer controlled_buffer_1
  one_byte_ram one_byte_ram_1 (
    .y(decoder_1_out0), .x(decoder_2_out0), .bus_set(bus_set), .bus_enable(bus_enable),
    .bus_input(controlled_buffer_1_out), .bus_output(controlled_buffer_1_out));
  one_byte_ram one_byte_ram_2 (
    .y(decoder_1_out1), .x(decoder_2_out0), .bus_set(bus_set), .bus_enable(bus_enable),
    .bus_input(controlled_buffer_1_out), .bus_output(controlled_buffer_1_out));
  one_byte_ram one_byte_ram_3 (
    .y(decoder_1_out2), .x(decoder_2_out0), .bus_set(bus_set), .bus_enable(bus_enable),
    .bus_input(controlled_buffer_1_out), .bus_output(controlled_buffer_1_out));
  one_byte_ram one_byte_ram_4 (
    .y(decoder_1_out3), .x(decoder_2_out0), .bus_set(bus_set), .bus_enable(bus_enable),
    .bus_input(controlled_buffer_1_out), .bus_output(controlled_buffer_1_out));
  one_byte_ram one_byte_ram_5 (
    .y(decoder_1_out4), .x(decoder_2_out0), .bus_set(bus_set), .bus_enable(bus_enable),
    .bus_input(controlled_buffer_1_out), .bus_output(controlled_buffer_1_out));
  one_byte_ram one_byte_ram_6 (
    .y(decoder_1_out5), .x(decoder_2_out0), .bus_set(bus_set), .bus_enable(bus_enable),
    .bus_input(controlled_buffer_1_out), .bus_output(controlled_buffer_1_out));
  one_byte_ram one_byte_ram_7 (
    .y(decoder_1_out6), .x(decoder_2_out0), .bus_set(bus_set), .bus_enable(bus_enable),
    .bus_input(controlled_buffer_1_out), .bus_output(controlled_buffer_1_out));
  one_byte_ram one_byte_ram_8 (
    .y(decoder_1_out7), .x(decoder_2_out0), .bus_set(bus_set), .bus_enable(bus_enable),
    .bus_input(controlled_buffer_1_out), .bus_output(controlled_buffer_1_out));
  one_byte_ram one_byte_ram_9 (
    .y(decoder_1_out8), .x(decoder_2_out0), .bus_set(bus_set), .bus_enable(bus_enable),
    .bus_input(controlled_buffer_1_out), .bus_output(controlled_buffer_1_out));
  one_byte_ram one_byte_ram_10 (
    .y(decoder_1_out9), .x(decoder_2_out0), .bus_set(bus_set), .bus_enable(bus_enable),
    .bus_input(controlled_buffer_1_out), .bus_output(controlled_buffer_1_out));
  one_byte_ram one_byte_ram_11 (
    .y(decoder_1_out8), .x(decoder_2_out0), .bus_set(bus_set), .bus_enable(bus_enable),
    .bus_input(controlled_buffer_1_out), .bus_output(controlled_buffer_1_out));
  one_byte_ram one_byte_ram_12 (
    .y(decoder_1_out11), .x(decoder_2_out0), .bus_set(bus_set), .bus_enable(bus_enable),
    .bus_input(controlled_buffer_1_out), .bus_output(controlled_buffer_1_out));
  one_byte_ram one_byte_ram_13 (
    .y(decoder_1_out12), .x(decoder_2_out0), .bus_set(bus_set), .bus_enable(bus_enable),
    .bus_input(controlled_buffer_1_out), .bus_output(controlled_buffer_1_out));
  one_byte_ram one_byte_ram_14 (
    .y(decoder_1_out13), .x(decoder_2_out0), .bus_set(bus_set), .bus_enable(bus_enable),
    .bus_input(controlled_buffer_1_out), .bus_output(controlled_buffer_1_out));
  one_byte_ram one_byte_ram_15 (
    .y(decoder_1_out14), .x(decoder_2_out0), .bus_set(bus_set), .bus_enable(bus_enable),
    .bus_input(controlled_buffer_1_out), .bus_output(controlled_buffer_1_out));
  one_byte_ram one_byte_ram_16 (
    .y(decoder_1_out15), .x(decoder_2_out0), .bus_set(bus_set), .bus_enable(bus_enable),
    .bus_input(controlled_buffer_1_out), .bus_output(controlled_buffer_1_out));
  Decoder #(.enable("false"), .select(4)) decoder_2 (
    .out0(decoder_2_out0), .out1(decoder_2_out1), .out2(decoder_2_out2), .out3(decoder_2_out3),
    .out4(decoder_2_out4), .out5(decoder_2_out5), .out6(decoder_2_out6), .out7(decoder_2_out7),
    .out8(decoder_2_out8), .out9(decoder_2_out9), .out10(decoder_2_out10), .out11(decoder_2_out11),
    .out12(decoder_2_out12), .out13(decoder_2_out13), .out14(decoder_2_out14), .out15(decoder_2_out15),
    .sel(eight_bit_register_1_o[3:0]));
  one_byte_ram one_byte_ram_17 (
    .y(decoder_1_out0), .x(decoder_2_out1), .bus_set(bus_set), .bus_enable(bus_enable),
    .bus_input(controlled_buffer_1_out), .bus_output(controlled_buffer_1_out));
  one_byte_ram one_byte_ram_18 (
    .y(decoder_1_out1), .x(decoder_2_out1), .bus_set(bus_set), .bus_enable(bus_enable),
    .bus_input(controlled_buffer_1_out), .bus_output(controlled_buffer_1_out));
  one_byte_ram one_byte_ram_19 (
    .y(decoder_1_out2), .x(decoder_2_out1), .bus_set(bus_set), .bus_enable(bus_enable),
    .bus_input(controlled_buffer_1_out), .bus_output(controlled_buffer_1_out));
  one_byte_ram one_byte_ram_20 (
    .y(decoder_1_out3), .x(decoder_2_out1), .bus_set(bus_set), .bus_enable(bus_enable),
    .bus_input(controlled_buffer_1_out), .bus_output(controlled_buffer_1_out));
  one_byte_ram one_byte_ram_21 (
    .y(decoder_1_out4), .x(decoder_2_out1), .bus_set(bus_set), .bus_enable(bus_enable),
    .bus_input(controlled_buffer_1_out), .bus_output(controlled_buffer_1_out));
  one_byte_ram one_byte_ram_22 (
    .y(decoder_1_out5), .x(decoder_2_out1), .bus_set(bus_set), .bus_enable(bus_enable),
    .bus_input(controlled_buffer_1_out), .bus_output(controlled_buffer_1_out));
  one_byte_ram one_byte_ram_23 (
    .y(decoder_1_out6), .x(decoder_2_out1), .bus_set(bus_set), .bus_enable(bus_enable),
    .bus_input(controlled_buffer_1_out), .bus_output(controlled_buffer_1_out));
  one_byte_ram one_byte_ram_24 (
    .y(decoder_1_out7), .x(decoder_2_out1), .bus_set(bus_set), .bus_enable(bus_enable),
    .bus_input(controlled_buffer_1_out), .bus_output(controlled_buffer_1_out));
  one_byte_ram one_byte_ram_25 (
    .y(decoder_1_out8), .x(decoder_2_out1), .bus_set(bus_set), .bus_enable(bus_enable),
    .bus_input(controlled_buffer_1_out), .bus_output(controlled_buffer_1_out));
  one_byte_ram one_byte_ram_26 (
    .y(decoder_1_out9), .x(decoder_2_out1), .bus_set(bus_set), .bus_enable(bus_enable),
    .bus_input(controlled_buffer_1_out), .bus_output(controlled_buffer_1_out));
  one_byte_ram one_byte_ram_27 (
    .y(decoder_1_out8), .x(decoder_2_out1), .bus_set(bus_set), .bus_enable(bus_enable),
    .bus_input(controlled_buffer_1_out), .bus_output(controlled_buffer_1_out));
  one_byte_ram one_byte_ram_28 (
    .y(decoder_1_out11), .x(decoder_2_out1), .bus_set(bus_set), .bus_enable(bus_enable),
    .bus_input(controlled_buffer_1_out), .bus_output(controlled_buffer_1_out));
  one_byte_ram one_byte_ram_29 (
    .y(decoder_1_out12), .x(decoder_2_out1), .bus_set(bus_set), .bus_enable(bus_enable),
    .bus_input(controlled_buffer_1_out), .bus_output(controlled_buffer_1_out));
  one_byte_ram one_byte_ram_30 (
    .y(decoder_1_out13), .x(decoder_2_out1), .bus_set(bus_set), .bus_enable(bus_enable),
    .bus_input(controlled_buffer_1_out), .bus_output(controlled_buffer_1_out));
  one_byte_ram one_byte_ram_31 (
    .y(decoder_1_out14), .x(decoder_2_out1), .bus_set(bus_set), .bus_enable(bus_enable),
    .bus_input(controlled_buffer_1_out), .bus_output(controlled_buffer_1_out));
  one_byte_ram one_byte_ram_32 (
    .y(decoder_1_out15), .x(decoder_2_out1), .bus_set(bus_set), .bus_enable(bus_enable),
    .bus_input(controlled_buffer_1_out), .bus_output(controlled_buffer_1_out));
  one_byte_ram one_byte_ram_33 (
    .y(decoder_1_out0), .x(decoder_2_out2), .bus_set(bus_set), .bus_enable(bus_enable),
    .bus_input(controlled_buffer_1_out), .bus_output(controlled_buffer_1_out));
  one_byte_ram one_byte_ram_34 (
    .y(decoder_1_out1), .x(decoder_2_out2), .bus_set(bus_set), .bus_enable(bus_enable),
    .bus_input(controlled_buffer_1_out), .bus_output(controlled_buffer_1_out));
  one_byte_ram one_byte_ram_35 (
    .y(decoder_1_out2), .x(decoder_2_out2), .bus_set(bus_set), .bus_enable(bus_enable),
    .bus_input(controlled_buffer_1_out), .bus_output(controlled_buffer_1_out));
  one_byte_ram one_byte_ram_36 (
    .y(decoder_1_out3), .x(decoder_2_out2), .bus_set(bus_set), .bus_enable(bus_enable),
    .bus_input(controlled_buffer_1_out), .bus_output(controlled_buffer_1_out));
  one_byte_ram one_byte_ram_37 (
    .y(decoder_1_out4), .x(decoder_2_out2), .bus_set(bus_set), .bus_enable(bus_enable),
    .bus_input(controlled_buffer_1_out), .bus_output(controlled_buffer_1_out));
  one_byte_ram one_byte_ram_38 (
    .y(decoder_1_out5), .x(decoder_2_out2), .bus_set(bus_set), .bus_enable(bus_enable),
    .bus_input(controlled_buffer_1_out), .bus_output(controlled_buffer_1_out));
  one_byte_ram one_byte_ram_39 (
    .y(decoder_1_out6), .x(decoder_2_out2), .bus_set(bus_set), .bus_enable(bus_enable),
    .bus_input(controlled_buffer_1_out), .bus_output(controlled_buffer_1_out));
  one_byte_ram one_byte_ram_40 (
    .y(decoder_1_out7), .x(decoder_2_out2), .bus_set(bus_set), .bus_enable(bus_enable),
    .bus_input(controlled_buffer_1_out), .bus_output(controlled_buffer_1_out));
  one_byte_ram one_byte_ram_41 (
    .y(decoder_1_out8), .x(decoder_2_out2), .bus_set(bus_set), .bus_enable(bus_enable),
    .bus_input(controlled_buffer_1_out), .bus_output(controlled_buffer_1_out));
  one_byte_ram one_byte_ram_42 (
    .y(decoder_1_out9), .x(decoder_2_out2), .bus_set(bus_set), .bus_enable(bus_enable),
    .bus_input(controlled_buffer_1_out), .bus_output(controlled_buffer_1_out));
  one_byte_ram one_byte_ram_43 (
    .y(decoder_1_out8), .x(decoder_2_out2), .bus_set(bus_set), .bus_enable(bus_enable),
    .bus_input(controlled_buffer_1_out), .bus_output(controlled_buffer_1_out));
  one_byte_ram one_byte_ram_44 (
    .y(decoder_1_out11), .x(decoder_2_out2), .bus_set(bus_set), .bus_enable(bus_enable),
    .bus_input(controlled_buffer_1_out), .bus_output(controlled_buffer_1_out));
  one_byte_ram one_byte_ram_45 (
    .y(decoder_1_out12), .x(decoder_2_out2), .bus_set(bus_set), .bus_enable(bus_enable),
    .bus_input(controlled_buffer_1_out), .bus_output(controlled_buffer_1_out));
  one_byte_ram one_byte_ram_46 (
    .y(decoder_1_out13), .x(decoder_2_out2), .bus_set(bus_set), .bus_enable(bus_enable),
    .bus_input(controlled_buffer_1_out), .bus_output(controlled_buffer_1_out));
  one_byte_ram one_byte_ram_47 (
    .y(decoder_1_out14), .x(decoder_2_out2), .bus_set(bus_set), .bus_enable(bus_enable),
    .bus_input(controlled_buffer_1_out), .bus_output(controlled_buffer_1_out));
  one_byte_ram one_byte_ram_48 (
    .y(decoder_1_out15), .x(decoder_2_out2), .bus_set(bus_set), .bus_enable(bus_enable),
    .bus_input(controlled_buffer_1_out), .bus_output(controlled_buffer_1_out));
  one_byte_ram one_byte_ram_49 (
    .y(decoder_1_out0), .x(decoder_2_out3), .bus_set(bus_set), .bus_enable(bus_enable),
    .bus_input(controlled_buffer_1_out), .bus_output(controlled_buffer_1_out));
  one_byte_ram one_byte_ram_50 (
    .y(decoder_1_out1), .x(decoder_2_out3), .bus_set(bus_set), .bus_enable(bus_enable),
    .bus_input(controlled_buffer_1_out), .bus_output(controlled_buffer_1_out));
  one_byte_ram one_byte_ram_51 (
    .y(decoder_1_out2), .x(decoder_2_out3), .bus_set(bus_set), .bus_enable(bus_enable),
    .bus_input(controlled_buffer_1_out), .bus_output(controlled_buffer_1_out));
  one_byte_ram one_byte_ram_52 (
    .y(decoder_1_out3), .x(decoder_2_out3), .bus_set(bus_set), .bus_enable(bus_enable),
    .bus_input(controlled_buffer_1_out), .bus_output(controlled_buffer_1_out));
  one_byte_ram one_byte_ram_53 (
    .y(decoder_1_out4), .x(decoder_2_out3), .bus_set(bus_set), .bus_enable(bus_enable),
    .bus_input(controlled_buffer_1_out), .bus_output(controlled_buffer_1_out));
  one_byte_ram one_byte_ram_54 (
    .y(decoder_1_out5), .x(decoder_2_out3), .bus_set(bus_set), .bus_enable(bus_enable),
    .bus_input(controlled_buffer_1_out), .bus_output(controlled_buffer_1_out));
  one_byte_ram one_byte_ram_55 (
    .y(decoder_1_out6), .x(decoder_2_out3), .bus_set(bus_set), .bus_enable(bus_enable),
    .bus_input(controlled_buffer_1_out), .bus_output(controlled_buffer_1_out));
  one_byte_ram one_byte_ram_56 (
    .y(decoder_1_out7), .x(decoder_2_out3), .bus_set(bus_set), .bus_enable(bus_enable),
    .bus_input(controlled_buffer_1_out), .bus_output(controlled_buffer_1_out));
  one_byte_ram one_byte_ram_57 (
    .y(decoder_1_out8), .x(decoder_2_out3), .bus_set(bus_set), .bus_enable(bus_enable),
    .bus_input(controlled_buffer_1_out), .bus_output(controlled_buffer_1_out));
  one_byte_ram one_byte_ram_58 (
    .y(decoder_1_out9), .x(decoder_2_out3), .bus_set(bus_set), .bus_enable(bus_enable),
    .bus_input(controlled_buffer_1_out), .bus_output(controlled_buffer_1_out));
  one_byte_ram one_byte_ram_59 (
    .y(decoder_1_out8), .x(decoder_2_out3), .bus_set(bus_set), .bus_enable(bus_enable),
    .bus_input(controlled_buffer_1_out), .bus_output(controlled_buffer_1_out));
  one_byte_ram one_byte_ram_60 (
    .y(decoder_1_out11), .x(decoder_2_out3), .bus_set(bus_set), .bus_enable(bus_enable),
    .bus_input(controlled_buffer_1_out), .bus_output(controlled_buffer_1_out));
  one_byte_ram one_byte_ram_61 (
    .y(decoder_1_out12), .x(decoder_2_out3), .bus_set(bus_set), .bus_enable(bus_enable),
    .bus_input(controlled_buffer_1_out), .bus_output(controlled_buffer_1_out));
  one_byte_ram one_byte_ram_62 (
    .y(decoder_1_out13), .x(decoder_2_out3), .bus_set(bus_set), .bus_enable(bus_enable),
    .bus_input(controlled_buffer_1_out), .bus_output(controlled_buffer_1_out));
  one_byte_ram one_byte_ram_63 (
    .y(decoder_1_out14), .x(decoder_2_out3), .bus_set(bus_set), .bus_enable(bus_enable),
    .bus_input(controlled_buffer_1_out), .bus_output(controlled_buffer_1_out));
  one_byte_ram one_byte_ram_64 (
    .y(decoder_1_out15), .x(decoder_2_out3), .bus_set(bus_set), .bus_enable(bus_enable),
    .bus_input(controlled_buffer_1_out), .bus_output(controlled_buffer_1_out));
  one_byte_ram one_byte_ram_65 (
    .y(decoder_1_out0), .x(decoder_2_out4), .bus_set(bus_set), .bus_enable(bus_enable),
    .bus_input(controlled_buffer_1_out), .bus_output(controlled_buffer_1_out));
  one_byte_ram one_byte_ram_66 (
    .y(decoder_1_out1), .x(decoder_2_out4), .bus_set(bus_set), .bus_enable(bus_enable),
    .bus_input(controlled_buffer_1_out), .bus_output(controlled_buffer_1_out));
  one_byte_ram one_byte_ram_67 (
    .y(decoder_1_out2), .x(decoder_2_out4), .bus_set(bus_set), .bus_enable(bus_enable),
    .bus_input(controlled_buffer_1_out), .bus_output(controlled_buffer_1_out));
  one_byte_ram one_byte_ram_68 (
    .y(decoder_1_out3), .x(decoder_2_out4), .bus_set(bus_set), .bus_enable(bus_enable),
    .bus_input(controlled_buffer_1_out), .bus_output(controlled_buffer_1_out));
  one_byte_ram one_byte_ram_69 (
    .y(decoder_1_out4), .x(decoder_2_out4), .bus_set(bus_set), .bus_enable(bus_enable),
    .bus_input(controlled_buffer_1_out), .bus_output(controlled_buffer_1_out));
  one_byte_ram one_byte_ram_70 (
    .y(decoder_1_out5), .x(decoder_2_out4), .bus_set(bus_set), .bus_enable(bus_enable),
    .bus_input(controlled_buffer_1_out), .bus_output(controlled_buffer_1_out));
  one_byte_ram one_byte_ram_71 (
    .y(decoder_1_out6), .x(decoder_2_out4), .bus_set(bus_set), .bus_enable(bus_enable),
    .bus_input(controlled_buffer_1_out), .bus_output(controlled_buffer_1_out));
  one_byte_ram one_byte_ram_72 (
    .y(decoder_1_out7), .x(decoder_2_out4), .bus_set(bus_set), .bus_enable(bus_enable),
    .bus_input(controlled_buffer_1_out), .bus_output(controlled_buffer_1_out));
  one_byte_ram one_byte_ram_73 (
    .y(decoder_1_out8), .x(decoder_2_out4), .bus_set(bus_set), .bus_enable(bus_enable),
    .bus_input(controlled_buffer_1_out), .bus_output(controlled_buffer_1_out));
  one_byte_ram one_byte_ram_74 (
    .y(decoder_1_out9), .x(decoder_2_out4), .bus_set(bus_set), .bus_enable(bus_enable),
    .bus_input(controlled_buffer_1_out), .bus_output(controlled_buffer_1_out));
  one_byte_ram one_byte_ram_75 (
    .y(decoder_1_out8), .x(decoder_2_out4), .bus_set(bus_set), .bus_enable(bus_enable),
    .bus_input(controlled_buffer_1_out), .bus_output(controlled_buffer_1_out));
  one_byte_ram one_byte_ram_76 (
    .y(decoder_1_out11), .x(decoder_2_out4), .bus_set(bus_set), .bus_enable(bus_enable),
    .bus_input(controlled_buffer_1_out), .bus_output(controlled_buffer_1_out));
  one_byte_ram one_byte_ram_77 (
    .y(decoder_1_out12), .x(decoder_2_out4), .bus_set(bus_set), .bus_enable(bus_enable),
    .bus_input(controlled_buffer_1_out), .bus_output(controlled_buffer_1_out));
  one_byte_ram one_byte_ram_78 (
    .y(decoder_1_out13), .x(decoder_2_out4), .bus_set(bus_set), .bus_enable(bus_enable),
    .bus_input(controlled_buffer_1_out), .bus_output(controlled_buffer_1_out));
  one_byte_ram one_byte_ram_79 (
    .y(decoder_1_out14), .x(decoder_2_out4), .bus_set(bus_set), .bus_enable(bus_enable),
    .bus_input(controlled_buffer_1_out), .bus_output(controlled_buffer_1_out));
  one_byte_ram one_byte_ram_80 (
    .y(decoder_1_out15), .x(decoder_2_out4), .bus_set(bus_set), .bus_enable(bus_enable),
    .bus_input(controlled_buffer_1_out), .bus_output(controlled_buffer_1_out));
  one_byte_ram one_byte_ram_81 (
    .y(decoder_1_out0), .x(decoder_2_out5), .bus_set(bus_set), .bus_enable(bus_enable),
    .bus_input(controlled_buffer_1_out), .bus_output(controlled_buffer_1_out));
  one_byte_ram one_byte_ram_82 (
    .y(decoder_1_out1), .x(decoder_2_out5), .bus_set(bus_set), .bus_enable(bus_enable),
    .bus_input(controlled_buffer_1_out), .bus_output(controlled_buffer_1_out));
  one_byte_ram one_byte_ram_83 (
    .y(decoder_1_out2), .x(decoder_2_out5), .bus_set(bus_set), .bus_enable(bus_enable),
    .bus_input(controlled_buffer_1_out), .bus_output(controlled_buffer_1_out));
  one_byte_ram one_byte_ram_84 (
    .y(decoder_1_out3), .x(decoder_2_out5), .bus_set(bus_set), .bus_enable(bus_enable),
    .bus_input(controlled_buffer_1_out), .bus_output(controlled_buffer_1_out));
  one_byte_ram one_byte_ram_85 (
    .y(decoder_1_out4), .x(decoder_2_out5), .bus_set(bus_set), .bus_enable(bus_enable),
    .bus_input(controlled_buffer_1_out), .bus_output(controlled_buffer_1_out));
  one_byte_ram one_byte_ram_86 (
    .y(decoder_1_out5), .x(decoder_2_out5), .bus_set(bus_set), .bus_enable(bus_enable),
    .bus_input(controlled_buffer_1_out), .bus_output(controlled_buffer_1_out));
  one_byte_ram one_byte_ram_87 (
    .y(decoder_1_out6), .x(decoder_2_out5), .bus_set(bus_set), .bus_enable(bus_enable),
    .bus_input(controlled_buffer_1_out), .bus_output(controlled_buffer_1_out));
  one_byte_ram one_byte_ram_88 (
    .y(decoder_1_out7), .x(decoder_2_out5), .bus_set(bus_set), .bus_enable(bus_enable),
    .bus_input(controlled_buffer_1_out), .bus_output(controlled_buffer_1_out));
  one_byte_ram one_byte_ram_89 (
    .y(decoder_1_out8), .x(decoder_2_out5), .bus_set(bus_set), .bus_enable(bus_enable),
    .bus_input(controlled_buffer_1_out), .bus_output(controlled_buffer_1_out));
  one_byte_ram one_byte_ram_90 (
    .y(decoder_1_out9), .x(decoder_2_out5), .bus_set(bus_set), .bus_enable(bus_enable),
    .bus_input(controlled_buffer_1_out), .bus_output(controlled_buffer_1_out));
  one_byte_ram one_byte_ram_91 (
    .y(decoder_1_out8), .x(decoder_2_out5), .bus_set(bus_set), .bus_enable(bus_enable),
    .bus_input(controlled_buffer_1_out), .bus_output(controlled_buffer_1_out));
  one_byte_ram one_byte_ram_92 (
    .y(decoder_1_out11), .x(decoder_2_out5), .bus_set(bus_set), .bus_enable(bus_enable),
    .bus_input(controlled_buffer_1_out), .bus_output(controlled_buffer_1_out));
  one_byte_ram one_byte_ram_93 (
    .y(decoder_1_out12), .x(decoder_2_out5), .bus_set(bus_set), .bus_enable(bus_enable),
    .bus_input(controlled_buffer_1_out), .bus_output(controlled_buffer_1_out));
  one_byte_ram one_byte_ram_94 (
    .y(decoder_1_out13), .x(decoder_2_out5), .bus_set(bus_set), .bus_enable(bus_enable),
    .bus_input(controlled_buffer_1_out), .bus_output(controlled_buffer_1_out));
  one_byte_ram one_byte_ram_95 (
    .y(decoder_1_out14), .x(decoder_2_out5), .bus_set(bus_set), .bus_enable(bus_enable),
    .bus_input(controlled_buffer_1_out), .bus_output(controlled_buffer_1_out));
  one_byte_ram one_byte_ram_96 (
    .y(decoder_1_out15), .x(decoder_2_out5), .bus_set(bus_set), .bus_enable(bus_enable),
    .bus_input(controlled_buffer_1_out), .bus_output(controlled_buffer_1_out));
  one_byte_ram one_byte_ram_97 (
    .y(decoder_1_out0), .x(decoder_2_out6), .bus_set(bus_set), .bus_enable(bus_enable),
    .bus_input(controlled_buffer_1_out), .bus_output(controlled_buffer_1_out));
  one_byte_ram one_byte_ram_98 (
    .y(decoder_1_out1), .x(decoder_2_out6), .bus_set(bus_set), .bus_enable(bus_enable),
    .bus_input(controlled_buffer_1_out), .bus_output(controlled_buffer_1_out));
  one_byte_ram one_byte_ram_99 (
    .y(decoder_1_out2), .x(decoder_2_out6), .bus_set(bus_set), .bus_enable(bus_enable),
    .bus_input(controlled_buffer_1_out), .bus_output(controlled_buffer_1_out));
  one_byte_ram one_byte_ram_100 (
    .y(decoder_1_out3), .x(decoder_2_out6), .bus_set(bus_set), .bus_enable(bus_enable),
    .bus_input(controlled_buffer_1_out), .bus_output(controlled_buffer_1_out));
  one_byte_ram one_byte_ram_101 (
    .y(decoder_1_out4), .x(decoder_2_out6), .bus_set(bus_set), .bus_enable(bus_enable),
    .bus_input(controlled_buffer_1_out), .bus_output(controlled_buffer_1_out));
  one_byte_ram one_byte_ram_102 (
    .y(decoder_1_out5), .x(decoder_2_out6), .bus_set(bus_set), .bus_enable(bus_enable),
    .bus_input(controlled_buffer_1_out), .bus_output(controlled_buffer_1_out));
  one_byte_ram one_byte_ram_103 (
    .y(decoder_1_out6), .x(decoder_2_out6), .bus_set(bus_set), .bus_enable(bus_enable),
    .bus_input(controlled_buffer_1_out), .bus_output(controlled_buffer_1_out));
  one_byte_ram one_byte_ram_104 (
    .y(decoder_1_out7), .x(decoder_2_out6), .bus_set(bus_set), .bus_enable(bus_enable),
    .bus_input(controlled_buffer_1_out), .bus_output(controlled_buffer_1_out));
  one_byte_ram one_byte_ram_105 (
    .y(decoder_1_out8), .x(decoder_2_out6), .bus_set(bus_set), .bus_enable(bus_enable),
    .bus_input(controlled_buffer_1_out), .bus_output(controlled_buffer_1_out));
  one_byte_ram one_byte_ram_106 (
    .y(decoder_1_out9), .x(decoder_2_out6), .bus_set(bus_set), .bus_enable(bus_enable),
    .bus_input(controlled_buffer_1_out), .bus_output(controlled_buffer_1_out));
  one_byte_ram one_byte_ram_107 (
    .y(decoder_1_out8), .x(decoder_2_out6), .bus_set(bus_set), .bus_enable(bus_enable),
    .bus_input(controlled_buffer_1_out), .bus_output(controlled_buffer_1_out));
  one_byte_ram one_byte_ram_108 (
    .y(decoder_1_out11), .x(decoder_2_out6), .bus_set(bus_set), .bus_enable(bus_enable),
    .bus_input(controlled_buffer_1_out), .bus_output(controlled_buffer_1_out));
  one_byte_ram one_byte_ram_109 (
    .y(decoder_1_out12), .x(decoder_2_out6), .bus_set(bus_set), .bus_enable(bus_enable),
    .bus_input(controlled_buffer_1_out), .bus_output(controlled_buffer_1_out));
  one_byte_ram one_byte_ram_110 (
    .y(decoder_1_out13), .x(decoder_2_out6), .bus_set(bus_set), .bus_enable(bus_enable),
    .bus_input(controlled_buffer_1_out), .bus_output(controlled_buffer_1_out));
  one_byte_ram one_byte_ram_111 (
    .y(decoder_1_out14), .x(decoder_2_out6), .bus_set(bus_set), .bus_enable(bus_enable),
    .bus_input(controlled_buffer_1_out), .bus_output(controlled_buffer_1_out));
  one_byte_ram one_byte_ram_112 (
    .y(decoder_1_out15), .x(decoder_2_out6), .bus_set(bus_set), .bus_enable(bus_enable),
    .bus_input(controlled_buffer_1_out), .bus_output(controlled_buffer_1_out));
  one_byte_ram one_byte_ram_113 (
    .y(decoder_1_out0), .x(decoder_2_out7), .bus_set(bus_set), .bus_enable(bus_enable),
    .bus_input(controlled_buffer_1_out), .bus_output(controlled_buffer_1_out));
  one_byte_ram one_byte_ram_114 (
    .y(decoder_1_out1), .x(decoder_2_out7), .bus_set(bus_set), .bus_enable(bus_enable),
    .bus_input(controlled_buffer_1_out), .bus_output(controlled_buffer_1_out));
  one_byte_ram one_byte_ram_115 (
    .y(decoder_1_out2), .x(decoder_2_out7), .bus_set(bus_set), .bus_enable(bus_enable),
    .bus_input(controlled_buffer_1_out), .bus_output(controlled_buffer_1_out));
  one_byte_ram one_byte_ram_116 (
    .y(decoder_1_out3), .x(decoder_2_out7), .bus_set(bus_set), .bus_enable(bus_enable),
    .bus_input(controlled_buffer_1_out), .bus_output(controlled_buffer_1_out));
  one_byte_ram one_byte_ram_117 (
    .y(decoder_1_out4), .x(decoder_2_out7), .bus_set(bus_set), .bus_enable(bus_enable),
    .bus_input(controlled_buffer_1_out), .bus_output(controlled_buffer_1_out));
  one_byte_ram one_byte_ram_118 (
    .y(decoder_1_out5), .x(decoder_2_out7), .bus_set(bus_set), .bus_enable(bus_enable),
    .bus_input(controlled_buffer_1_out), .bus_output(controlled_buffer_1_out));
  one_byte_ram one_byte_ram_119 (
    .y(decoder_1_out6), .x(decoder_2_out7), .bus_set(bus_set), .bus_enable(bus_enable),
    .bus_input(controlled_buffer_1_out), .bus_output(controlled_buffer_1_out));
  one_byte_ram one_byte_ram_120 (
    .y(decoder_1_out7), .x(decoder_2_out7), .bus_set(bus_set), .bus_enable(bus_enable),
    .bus_input(controlled_buffer_1_out), .bus_output(controlled_buffer_1_out));
  one_byte_ram one_byte_ram_121 (
    .y(decoder_1_out8), .x(decoder_2_out7), .bus_set(bus_set), .bus_enable(bus_enable),
    .bus_input(controlled_buffer_1_out), .bus_output(controlled_buffer_1_out));
  one_byte_ram one_byte_ram_122 (
    .y(decoder_1_out9), .x(decoder_2_out7), .bus_set(bus_set), .bus_enable(bus_enable),
    .bus_input(controlled_buffer_1_out), .bus_output(controlled_buffer_1_out));
  one_byte_ram one_byte_ram_123 (
    .y(decoder_1_out8), .x(decoder_2_out7), .bus_set(bus_set), .bus_enable(bus_enable),
    .bus_input(controlled_buffer_1_out), .bus_output(controlled_buffer_1_out));
  one_byte_ram one_byte_ram_124 (
    .y(decoder_1_out11), .x(decoder_2_out7), .bus_set(bus_set), .bus_enable(bus_enable),
    .bus_input(controlled_buffer_1_out), .bus_output(controlled_buffer_1_out));
  one_byte_ram one_byte_ram_125 (
    .y(decoder_1_out12), .x(decoder_2_out7), .bus_set(bus_set), .bus_enable(bus_enable),
    .bus_input(controlled_buffer_1_out), .bus_output(controlled_buffer_1_out));
  one_byte_ram one_byte_ram_126 (
    .y(decoder_1_out13), .x(decoder_2_out7), .bus_set(bus_set), .bus_enable(bus_enable),
    .bus_input(controlled_buffer_1_out), .bus_output(controlled_buffer_1_out));
  one_byte_ram one_byte_ram_127 (
    .y(decoder_1_out14), .x(decoder_2_out7), .bus_set(bus_set), .bus_enable(bus_enable),
    .bus_input(controlled_buffer_1_out), .bus_output(controlled_buffer_1_out));
  one_byte_ram one_byte_ram_128 (
    .y(decoder_1_out15), .x(decoder_2_out7), .bus_set(bus_set), .bus_enable(bus_enable),
    .bus_input(controlled_buffer_1_out), .bus_output(controlled_buffer_1_out));
  one_byte_ram one_byte_ram_129 (
    .y(decoder_1_out0), .x(decoder_2_out8), .bus_set(bus_set), .bus_enable(bus_enable),
    .bus_input(controlled_buffer_1_out), .bus_output(controlled_buffer_1_out));
  one_byte_ram one_byte_ram_130 (
    .y(decoder_1_out1), .x(decoder_2_out8), .bus_set(bus_set), .bus_enable(bus_enable),
    .bus_input(controlled_buffer_1_out), .bus_output(controlled_buffer_1_out));
  one_byte_ram one_byte_ram_131 (
    .y(decoder_1_out2), .x(decoder_2_out8), .bus_set(bus_set), .bus_enable(bus_enable),
    .bus_input(controlled_buffer_1_out), .bus_output(controlled_buffer_1_out));
  one_byte_ram one_byte_ram_132 (
    .y(decoder_1_out3), .x(decoder_2_out8), .bus_set(bus_set), .bus_enable(bus_enable),
    .bus_input(controlled_buffer_1_out), .bus_output(controlled_buffer_1_out));
  one_byte_ram one_byte_ram_133 (
    .y(decoder_1_out4), .x(decoder_2_out8), .bus_set(bus_set), .bus_enable(bus_enable),
    .bus_input(controlled_buffer_1_out), .bus_output(controlled_buffer_1_out));
  one_byte_ram one_byte_ram_134 (
    .y(decoder_1_out5), .x(decoder_2_out8), .bus_set(bus_set), .bus_enable(bus_enable),
    .bus_input(controlled_buffer_1_out), .bus_output(controlled_buffer_1_out));
  one_byte_ram one_byte_ram_135 (
    .y(decoder_1_out6), .x(decoder_2_out8), .bus_set(bus_set), .bus_enable(bus_enable),
    .bus_input(controlled_buffer_1_out), .bus_output(controlled_buffer_1_out));
  one_byte_ram one_byte_ram_136 (
    .y(decoder_1_out7), .x(decoder_2_out8), .bus_set(bus_set), .bus_enable(bus_enable),
    .bus_input(controlled_buffer_1_out), .bus_output(controlled_buffer_1_out));
  one_byte_ram one_byte_ram_137 (
    .y(decoder_1_out8), .x(decoder_2_out8), .bus_set(bus_set), .bus_enable(bus_enable),
    .bus_input(controlled_buffer_1_out), .bus_output(controlled_buffer_1_out));
  one_byte_ram one_byte_ram_138 (
    .y(decoder_1_out9), .x(decoder_2_out8), .bus_set(bus_set), .bus_enable(bus_enable),
    .bus_input(controlled_buffer_1_out), .bus_output(controlled_buffer_1_out));
  one_byte_ram one_byte_ram_139 (
    .y(decoder_1_out8), .x(decoder_2_out8), .bus_set(bus_set), .bus_enable(bus_enable),
    .bus_input(controlled_buffer_1_out), .bus_output(controlled_buffer_1_out));
  one_byte_ram one_byte_ram_140 (
    .y(decoder_1_out11), .x(decoder_2_out8), .bus_set(bus_set), .bus_enable(bus_enable),
    .bus_input(controlled_buffer_1_out), .bus_output(controlled_buffer_1_out));
  one_byte_ram one_byte_ram_141 (
    .y(decoder_1_out12), .x(decoder_2_out8), .bus_set(bus_set), .bus_enable(bus_enable),
    .bus_input(controlled_buffer_1_out), .bus_output(controlled_buffer_1_out));
  one_byte_ram one_byte_ram_142 (
    .y(decoder_1_out13), .x(decoder_2_out8), .bus_set(bus_set), .bus_enable(bus_enable),
    .bus_input(controlled_buffer_1_out), .bus_output(controlled_buffer_1_out));
  one_byte_ram one_byte_ram_143 (
    .y(decoder_1_out14), .x(decoder_2_out8), .bus_set(bus_set), .bus_enable(bus_enable),
    .bus_input(controlled_buffer_1_out), .bus_output(controlled_buffer_1_out));
  one_byte_ram one_byte_ram_144 (
    .y(decoder_1_out15), .x(decoder_2_out8), .bus_set(bus_set), .bus_enable(bus_enable),
    .bus_input(controlled_buffer_1_out), .bus_output(controlled_buffer_1_out));
  one_byte_ram one_byte_ram_145 (
    .y(decoder_1_out0), .x(decoder_2_out9), .bus_set(bus_set), .bus_enable(bus_enable),
    .bus_input(controlled_buffer_1_out), .bus_output(controlled_buffer_1_out));
  one_byte_ram one_byte_ram_146 (
    .y(decoder_1_out1), .x(decoder_2_out9), .bus_set(bus_set), .bus_enable(bus_enable),
    .bus_input(controlled_buffer_1_out), .bus_output(controlled_buffer_1_out));
  one_byte_ram one_byte_ram_147 (
    .y(decoder_1_out2), .x(decoder_2_out9), .bus_set(bus_set), .bus_enable(bus_enable),
    .bus_input(controlled_buffer_1_out), .bus_output(controlled_buffer_1_out));
  one_byte_ram one_byte_ram_148 (
    .y(decoder_1_out3), .x(decoder_2_out9), .bus_set(bus_set), .bus_enable(bus_enable),
    .bus_input(controlled_buffer_1_out), .bus_output(controlled_buffer_1_out));
  one_byte_ram one_byte_ram_149 (
    .y(decoder_1_out4), .x(decoder_2_out9), .bus_set(bus_set), .bus_enable(bus_enable),
    .bus_input(controlled_buffer_1_out), .bus_output(controlled_buffer_1_out));
  one_byte_ram one_byte_ram_150 (
    .y(decoder_1_out5), .x(decoder_2_out9), .bus_set(bus_set), .bus_enable(bus_enable),
    .bus_input(controlled_buffer_1_out), .bus_output(controlled_buffer_1_out));
  one_byte_ram one_byte_ram_151 (
    .y(decoder_1_out6), .x(decoder_2_out9), .bus_set(bus_set), .bus_enable(bus_enable),
    .bus_input(controlled_buffer_1_out), .bus_output(controlled_buffer_1_out));
  one_byte_ram one_byte_ram_152 (
    .y(decoder_1_out7), .x(decoder_2_out9), .bus_set(bus_set), .bus_enable(bus_enable),
    .bus_input(controlled_buffer_1_out), .bus_output(controlled_buffer_1_out));
  one_byte_ram one_byte_ram_153 (
    .y(decoder_1_out8), .x(decoder_2_out9), .bus_set(bus_set), .bus_enable(bus_enable),
    .bus_input(controlled_buffer_1_out), .bus_output(controlled_buffer_1_out));
  one_byte_ram one_byte_ram_154 (
    .y(decoder_1_out9), .x(decoder_2_out9), .bus_set(bus_set), .bus_enable(bus_enable),
    .bus_input(controlled_buffer_1_out), .bus_output(controlled_buffer_1_out));
  one_byte_ram one_byte_ram_155 (
    .y(decoder_1_out8), .x(decoder_2_out9), .bus_set(bus_set), .bus_enable(bus_enable),
    .bus_input(controlled_buffer_1_out), .bus_output(controlled_buffer_1_out));
  one_byte_ram one_byte_ram_156 (
    .y(decoder_1_out11), .x(decoder_2_out9), .bus_set(bus_set), .bus_enable(bus_enable),
    .bus_input(controlled_buffer_1_out), .bus_output(controlled_buffer_1_out));
  one_byte_ram one_byte_ram_157 (
    .y(decoder_1_out12), .x(decoder_2_out9), .bus_set(bus_set), .bus_enable(bus_enable),
    .bus_input(controlled_buffer_1_out), .bus_output(controlled_buffer_1_out));
  one_byte_ram one_byte_ram_158 (
    .y(decoder_1_out13), .x(decoder_2_out9), .bus_set(bus_set), .bus_enable(bus_enable),
    .bus_input(controlled_buffer_1_out), .bus_output(controlled_buffer_1_out));
  one_byte_ram one_byte_ram_159 (
    .y(decoder_1_out14), .x(decoder_2_out9), .bus_set(bus_set), .bus_enable(bus_enable),
    .bus_input(controlled_buffer_1_out), .bus_output(controlled_buffer_1_out));
  one_byte_ram one_byte_ram_160 (
    .y(decoder_1_out15), .x(decoder_2_out9), .bus_set(bus_set), .bus_enable(bus_enable),
    .bus_input(controlled_buffer_1_out), .bus_output(controlled_buffer_1_out));
  one_byte_ram one_byte_ram_161 (
    .y(decoder_1_out0), .x(decoder_2_out10), .bus_set(bus_set), .bus_enable(bus_enable),
    .bus_input(controlled_buffer_1_out), .bus_output(controlled_buffer_1_out));
  one_byte_ram one_byte_ram_162 (
    .y(decoder_1_out1), .x(decoder_2_out10), .bus_set(bus_set), .bus_enable(bus_enable),
    .bus_input(controlled_buffer_1_out), .bus_output(controlled_buffer_1_out));
  one_byte_ram one_byte_ram_163 (
    .y(decoder_1_out2), .x(decoder_2_out10), .bus_set(bus_set), .bus_enable(bus_enable),
    .bus_input(controlled_buffer_1_out), .bus_output(controlled_buffer_1_out));
  one_byte_ram one_byte_ram_164 (
    .y(decoder_1_out3), .x(decoder_2_out10), .bus_set(bus_set), .bus_enable(bus_enable),
    .bus_input(controlled_buffer_1_out), .bus_output(controlled_buffer_1_out));
  one_byte_ram one_byte_ram_165 (
    .y(decoder_1_out4), .x(decoder_2_out10), .bus_set(bus_set), .bus_enable(bus_enable),
    .bus_input(controlled_buffer_1_out), .bus_output(controlled_buffer_1_out));
  one_byte_ram one_byte_ram_166 (
    .y(decoder_1_out5), .x(decoder_2_out10), .bus_set(bus_set), .bus_enable(bus_enable),
    .bus_input(controlled_buffer_1_out), .bus_output(controlled_buffer_1_out));
  one_byte_ram one_byte_ram_167 (
    .y(decoder_1_out6), .x(decoder_2_out10), .bus_set(bus_set), .bus_enable(bus_enable),
    .bus_input(controlled_buffer_1_out), .bus_output(controlled_buffer_1_out));
  one_byte_ram one_byte_ram_168 (
    .y(decoder_1_out7), .x(decoder_2_out10), .bus_set(bus_set), .bus_enable(bus_enable),
    .bus_input(controlled_buffer_1_out), .bus_output(controlled_buffer_1_out));
  one_byte_ram one_byte_ram_169 (
    .y(decoder_1_out8), .x(decoder_2_out10), .bus_set(bus_set), .bus_enable(bus_enable),
    .bus_input(controlled_buffer_1_out), .bus_output(controlled_buffer_1_out));
  one_byte_ram one_byte_ram_170 (
    .y(decoder_1_out9), .x(decoder_2_out10), .bus_set(bus_set), .bus_enable(bus_enable),
    .bus_input(controlled_buffer_1_out), .bus_output(controlled_buffer_1_out));
  one_byte_ram one_byte_ram_171 (
    .y(decoder_1_out8), .x(decoder_2_out10), .bus_set(bus_set), .bus_enable(bus_enable),
    .bus_input(controlled_buffer_1_out), .bus_output(controlled_buffer_1_out));
  one_byte_ram one_byte_ram_172 (
    .y(decoder_1_out11), .x(decoder_2_out10), .bus_set(bus_set), .bus_enable(bus_enable),
    .bus_input(controlled_buffer_1_out), .bus_output(controlled_buffer_1_out));
  one_byte_ram one_byte_ram_173 (
    .y(decoder_1_out12), .x(decoder_2_out10), .bus_set(bus_set), .bus_enable(bus_enable),
    .bus_input(controlled_buffer_1_out), .bus_output(controlled_buffer_1_out));
  one_byte_ram one_byte_ram_174 (
    .y(decoder_1_out13), .x(decoder_2_out10), .bus_set(bus_set), .bus_enable(bus_enable),
    .bus_input(controlled_buffer_1_out), .bus_output(controlled_buffer_1_out));
  one_byte_ram one_byte_ram_175 (
    .y(decoder_1_out14), .x(decoder_2_out10), .bus_set(bus_set), .bus_enable(bus_enable),
    .bus_input(controlled_buffer_1_out), .bus_output(controlled_buffer_1_out));
  one_byte_ram one_byte_ram_176 (
    .y(decoder_1_out15), .x(decoder_2_out10), .bus_set(bus_set), .bus_enable(bus_enable),
    .bus_input(controlled_buffer_1_out), .bus_output(controlled_buffer_1_out));
  one_byte_ram one_byte_ram_177 (
    .y(decoder_1_out0), .x(decoder_2_out11), .bus_set(bus_set), .bus_enable(bus_enable),
    .bus_input(controlled_buffer_1_out), .bus_output(controlled_buffer_1_out));
  one_byte_ram one_byte_ram_178 (
    .y(decoder_1_out1), .x(decoder_2_out11), .bus_set(bus_set), .bus_enable(bus_enable),
    .bus_input(controlled_buffer_1_out), .bus_output(controlled_buffer_1_out));
  one_byte_ram one_byte_ram_179 (
    .y(decoder_1_out2), .x(decoder_2_out11), .bus_set(bus_set), .bus_enable(bus_enable),
    .bus_input(controlled_buffer_1_out), .bus_output(controlled_buffer_1_out));
  one_byte_ram one_byte_ram_180 (
    .y(decoder_1_out3), .x(decoder_2_out11), .bus_set(bus_set), .bus_enable(bus_enable),
    .bus_input(controlled_buffer_1_out), .bus_output(controlled_buffer_1_out));
  one_byte_ram one_byte_ram_181 (
    .y(decoder_1_out4), .x(decoder_2_out11), .bus_set(bus_set), .bus_enable(bus_enable),
    .bus_input(controlled_buffer_1_out), .bus_output(controlled_buffer_1_out));
  one_byte_ram one_byte_ram_182 (
    .y(decoder_1_out5), .x(decoder_2_out11), .bus_set(bus_set), .bus_enable(bus_enable),
    .bus_input(controlled_buffer_1_out), .bus_output(controlled_buffer_1_out));
  one_byte_ram one_byte_ram_183 (
    .y(decoder_1_out6), .x(decoder_2_out11), .bus_set(bus_set), .bus_enable(bus_enable),
    .bus_input(controlled_buffer_1_out), .bus_output(controlled_buffer_1_out));
  one_byte_ram one_byte_ram_184 (
    .y(decoder_1_out7), .x(decoder_2_out11), .bus_set(bus_set), .bus_enable(bus_enable),
    .bus_input(controlled_buffer_1_out), .bus_output(controlled_buffer_1_out));
  one_byte_ram one_byte_ram_185 (
    .y(decoder_1_out8), .x(decoder_2_out11), .bus_set(bus_set), .bus_enable(bus_enable),
    .bus_input(controlled_buffer_1_out), .bus_output(controlled_buffer_1_out));
  one_byte_ram one_byte_ram_186 (
    .y(decoder_1_out9), .x(decoder_2_out11), .bus_set(bus_set), .bus_enable(bus_enable),
    .bus_input(controlled_buffer_1_out), .bus_output(controlled_buffer_1_out));
  one_byte_ram one_byte_ram_187 (
    .y(decoder_1_out8), .x(decoder_2_out11), .bus_set(bus_set), .bus_enable(bus_enable),
    .bus_input(controlled_buffer_1_out), .bus_output(controlled_buffer_1_out));
  one_byte_ram one_byte_ram_188 (
    .y(decoder_1_out11), .x(decoder_2_out11), .bus_set(bus_set), .bus_enable(bus_enable),
    .bus_input(controlled_buffer_1_out), .bus_output(controlled_buffer_1_out));
  one_byte_ram one_byte_ram_189 (
    .y(decoder_1_out12), .x(decoder_2_out11), .bus_set(bus_set), .bus_enable(bus_enable),
    .bus_input(controlled_buffer_1_out), .bus_output(controlled_buffer_1_out));
  one_byte_ram one_byte_ram_190 (
    .y(decoder_1_out13), .x(decoder_2_out11), .bus_set(bus_set), .bus_enable(bus_enable),
    .bus_input(controlled_buffer_1_out), .bus_output(controlled_buffer_1_out));
  one_byte_ram one_byte_ram_191 (
    .y(decoder_1_out14), .x(decoder_2_out11), .bus_set(bus_set), .bus_enable(bus_enable),
    .bus_input(controlled_buffer_1_out), .bus_output(controlled_buffer_1_out));
  one_byte_ram one_byte_ram_192 (
    .y(decoder_1_out15), .x(decoder_2_out11), .bus_set(bus_set), .bus_enable(bus_enable),
    .bus_input(controlled_buffer_1_out), .bus_output(controlled_buffer_1_out));
  one_byte_ram one_byte_ram_193 (
    .y(decoder_1_out0), .x(decoder_2_out12), .bus_set(bus_set), .bus_enable(bus_enable),
    .bus_input(controlled_buffer_1_out), .bus_output(controlled_buffer_1_out));
  one_byte_ram one_byte_ram_194 (
    .y(decoder_1_out1), .x(decoder_2_out12), .bus_set(bus_set), .bus_enable(bus_enable),
    .bus_input(controlled_buffer_1_out), .bus_output(controlled_buffer_1_out));
  one_byte_ram one_byte_ram_195 (
    .y(decoder_1_out2), .x(decoder_2_out12), .bus_set(bus_set), .bus_enable(bus_enable),
    .bus_input(controlled_buffer_1_out), .bus_output(controlled_buffer_1_out));
  one_byte_ram one_byte_ram_196 (
    .y(decoder_1_out3), .x(decoder_2_out12), .bus_set(bus_set), .bus_enable(bus_enable),
    .bus_input(controlled_buffer_1_out), .bus_output(controlled_buffer_1_out));
  one_byte_ram one_byte_ram_197 (
    .y(decoder_1_out4), .x(decoder_2_out12), .bus_set(bus_set), .bus_enable(bus_enable),
    .bus_input(controlled_buffer_1_out), .bus_output(controlled_buffer_1_out));
  one_byte_ram one_byte_ram_198 (
    .y(decoder_1_out5), .x(decoder_2_out12), .bus_set(bus_set), .bus_enable(bus_enable),
    .bus_input(controlled_buffer_1_out), .bus_output(controlled_buffer_1_out));
  one_byte_ram one_byte_ram_199 (
    .y(decoder_1_out6), .x(decoder_2_out12), .bus_set(bus_set), .bus_enable(bus_enable),
    .bus_input(controlled_buffer_1_out), .bus_output(controlled_buffer_1_out));
  one_byte_ram one_byte_ram_200 (
    .y(decoder_1_out7), .x(decoder_2_out12), .bus_set(bus_set), .bus_enable(bus_enable),
    .bus_input(controlled_buffer_1_out), .bus_output(controlled_buffer_1_out));
  one_byte_ram one_byte_ram_201 (
    .y(decoder_1_out8), .x(decoder_2_out12), .bus_set(bus_set), .bus_enable(bus_enable),
    .bus_input(controlled_buffer_1_out), .bus_output(controlled_buffer_1_out));
  one_byte_ram one_byte_ram_202 (
    .y(decoder_1_out9), .x(decoder_2_out12), .bus_set(bus_set), .bus_enable(bus_enable),
    .bus_input(controlled_buffer_1_out), .bus_output(controlled_buffer_1_out));
  one_byte_ram one_byte_ram_203 (
    .y(decoder_1_out8), .x(decoder_2_out12), .bus_set(bus_set), .bus_enable(bus_enable),
    .bus_input(controlled_buffer_1_out), .bus_output(controlled_buffer_1_out));
  one_byte_ram one_byte_ram_204 (
    .y(decoder_1_out11), .x(decoder_2_out12), .bus_set(bus_set), .bus_enable(bus_enable),
    .bus_input(controlled_buffer_1_out), .bus_output(controlled_buffer_1_out));
  one_byte_ram one_byte_ram_205 (
    .y(decoder_1_out12), .x(decoder_2_out12), .bus_set(bus_set), .bus_enable(bus_enable),
    .bus_input(controlled_buffer_1_out), .bus_output(controlled_buffer_1_out));
  one_byte_ram one_byte_ram_206 (
    .y(decoder_1_out13), .x(decoder_2_out12), .bus_set(bus_set), .bus_enable(bus_enable),
    .bus_input(controlled_buffer_1_out), .bus_output(controlled_buffer_1_out));
  one_byte_ram one_byte_ram_207 (
    .y(decoder_1_out14), .x(decoder_2_out12), .bus_set(bus_set), .bus_enable(bus_enable),
    .bus_input(controlled_buffer_1_out), .bus_output(controlled_buffer_1_out));
  one_byte_ram one_byte_ram_208 (
    .y(decoder_1_out15), .x(decoder_2_out12), .bus_set(bus_set), .bus_enable(bus_enable),
    .bus_input(controlled_buffer_1_out), .bus_output(controlled_buffer_1_out));
  one_byte_ram one_byte_ram_209 (
    .y(decoder_1_out0), .x(decoder_2_out13), .bus_set(bus_set), .bus_enable(bus_enable),
    .bus_input(controlled_buffer_1_out), .bus_output(controlled_buffer_1_out));
  one_byte_ram one_byte_ram_210 (
    .y(decoder_1_out1), .x(decoder_2_out13), .bus_set(bus_set), .bus_enable(bus_enable),
    .bus_input(controlled_buffer_1_out), .bus_output(controlled_buffer_1_out));
  one_byte_ram one_byte_ram_211 (
    .y(decoder_1_out2), .x(decoder_2_out13), .bus_set(bus_set), .bus_enable(bus_enable),
    .bus_input(controlled_buffer_1_out), .bus_output(controlled_buffer_1_out));
  one_byte_ram one_byte_ram_212 (
    .y(decoder_1_out3), .x(decoder_2_out13), .bus_set(bus_set), .bus_enable(bus_enable),
    .bus_input(controlled_buffer_1_out), .bus_output(controlled_buffer_1_out));
  one_byte_ram one_byte_ram_213 (
    .y(decoder_1_out4), .x(decoder_2_out13), .bus_set(bus_set), .bus_enable(bus_enable),
    .bus_input(controlled_buffer_1_out), .bus_output(controlled_buffer_1_out));
  one_byte_ram one_byte_ram_214 (
    .y(decoder_1_out5), .x(decoder_2_out13), .bus_set(bus_set), .bus_enable(bus_enable),
    .bus_input(controlled_buffer_1_out), .bus_output(controlled_buffer_1_out));
  one_byte_ram one_byte_ram_215 (
    .y(decoder_1_out6), .x(decoder_2_out13), .bus_set(bus_set), .bus_enable(bus_enable),
    .bus_input(controlled_buffer_1_out), .bus_output(controlled_buffer_1_out));
  one_byte_ram one_byte_ram_216 (
    .y(decoder_1_out7), .x(decoder_2_out13), .bus_set(bus_set), .bus_enable(bus_enable),
    .bus_input(controlled_buffer_1_out), .bus_output(controlled_buffer_1_out));
  one_byte_ram one_byte_ram_217 (
    .y(decoder_1_out8), .x(decoder_2_out13), .bus_set(bus_set), .bus_enable(bus_enable),
    .bus_input(controlled_buffer_1_out), .bus_output(controlled_buffer_1_out));
  one_byte_ram one_byte_ram_218 (
    .y(decoder_1_out9), .x(decoder_2_out13), .bus_set(bus_set), .bus_enable(bus_enable),
    .bus_input(controlled_buffer_1_out), .bus_output(controlled_buffer_1_out));
  one_byte_ram one_byte_ram_219 (
    .y(decoder_1_out8), .x(decoder_2_out13), .bus_set(bus_set), .bus_enable(bus_enable),
    .bus_input(controlled_buffer_1_out), .bus_output(controlled_buffer_1_out));
  one_byte_ram one_byte_ram_220 (
    .y(decoder_1_out11), .x(decoder_2_out13), .bus_set(bus_set), .bus_enable(bus_enable),
    .bus_input(controlled_buffer_1_out), .bus_output(controlled_buffer_1_out));
  one_byte_ram one_byte_ram_221 (
    .y(decoder_1_out12), .x(decoder_2_out13), .bus_set(bus_set), .bus_enable(bus_enable),
    .bus_input(controlled_buffer_1_out), .bus_output(controlled_buffer_1_out));
  one_byte_ram one_byte_ram_222 (
    .y(decoder_1_out13), .x(decoder_2_out13), .bus_set(bus_set), .bus_enable(bus_enable),
    .bus_input(controlled_buffer_1_out), .bus_output(controlled_buffer_1_out));
  one_byte_ram one_byte_ram_223 (
    .y(decoder_1_out14), .x(decoder_2_out13), .bus_set(bus_set), .bus_enable(bus_enable),
    .bus_input(controlled_buffer_1_out), .bus_output(controlled_buffer_1_out));
  one_byte_ram one_byte_ram_224 (
    .y(decoder_1_out15), .x(decoder_2_out13), .bus_set(bus_set), .bus_enable(bus_enable),
    .bus_input(controlled_buffer_1_out), .bus_output(controlled_buffer_1_out));
  one_byte_ram one_byte_ram_225 (
    .y(decoder_1_out0), .x(decoder_2_out14), .bus_set(bus_set), .bus_enable(bus_enable),
    .bus_input(controlled_buffer_1_out), .bus_output(controlled_buffer_1_out));
  one_byte_ram one_byte_ram_226 (
    .y(decoder_1_out1), .x(decoder_2_out14), .bus_set(bus_set), .bus_enable(bus_enable),
    .bus_input(controlled_buffer_1_out), .bus_output(controlled_buffer_1_out));
  one_byte_ram one_byte_ram_227 (
    .y(decoder_1_out2), .x(decoder_2_out14), .bus_set(bus_set), .bus_enable(bus_enable),
    .bus_input(controlled_buffer_1_out), .bus_output(controlled_buffer_1_out));
  one_byte_ram one_byte_ram_228 (
    .y(decoder_1_out3), .x(decoder_2_out14), .bus_set(bus_set), .bus_enable(bus_enable),
    .bus_input(controlled_buffer_1_out), .bus_output(controlled_buffer_1_out));
  one_byte_ram one_byte_ram_229 (
    .y(decoder_1_out4), .x(decoder_2_out14), .bus_set(bus_set), .bus_enable(bus_enable),
    .bus_input(controlled_buffer_1_out), .bus_output(controlled_buffer_1_out));
  one_byte_ram one_byte_ram_230 (
    .y(decoder_1_out5), .x(decoder_2_out14), .bus_set(bus_set), .bus_enable(bus_enable),
    .bus_input(controlled_buffer_1_out), .bus_output(controlled_buffer_1_out));
  one_byte_ram one_byte_ram_231 (
    .y(decoder_1_out6), .x(decoder_2_out14), .bus_set(bus_set), .bus_enable(bus_enable),
    .bus_input(controlled_buffer_1_out), .bus_output(controlled_buffer_1_out));
  one_byte_ram one_byte_ram_232 (
    .y(decoder_1_out7), .x(decoder_2_out14), .bus_set(bus_set), .bus_enable(bus_enable),
    .bus_input(controlled_buffer_1_out), .bus_output(controlled_buffer_1_out));
  one_byte_ram one_byte_ram_233 (
    .y(decoder_1_out8), .x(decoder_2_out14), .bus_set(bus_set), .bus_enable(bus_enable),
    .bus_input(controlled_buffer_1_out), .bus_output(controlled_buffer_1_out));
  one_byte_ram one_byte_ram_234 (
    .y(decoder_1_out9), .x(decoder_2_out14), .bus_set(bus_set), .bus_enable(bus_enable),
    .bus_input(controlled_buffer_1_out), .bus_output(controlled_buffer_1_out));
  one_byte_ram one_byte_ram_235 (
    .y(decoder_1_out8), .x(decoder_2_out14), .bus_set(bus_set), .bus_enable(bus_enable),
    .bus_input(controlled_buffer_1_out), .bus_output(controlled_buffer_1_out));
  one_byte_ram one_byte_ram_236 (
    .y(decoder_1_out11), .x(decoder_2_out14), .bus_set(bus_set), .bus_enable(bus_enable),
    .bus_input(controlled_buffer_1_out), .bus_output(controlled_buffer_1_out));
  one_byte_ram one_byte_ram_237 (
    .y(decoder_1_out12), .x(decoder_2_out14), .bus_set(bus_set), .bus_enable(bus_enable),
    .bus_input(controlled_buffer_1_out), .bus_output(controlled_buffer_1_out));
  one_byte_ram one_byte_ram_238 (
    .y(decoder_1_out13), .x(decoder_2_out14), .bus_set(bus_set), .bus_enable(bus_enable),
    .bus_input(controlled_buffer_1_out), .bus_output(controlled_buffer_1_out));
  one_byte_ram one_byte_ram_239 (
    .y(decoder_1_out14), .x(decoder_2_out14), .bus_set(bus_set), .bus_enable(bus_enable),
    .bus_input(controlled_buffer_1_out), .bus_output(controlled_buffer_1_out));
  one_byte_ram one_byte_ram_240 (
    .y(decoder_1_out15), .x(decoder_2_out14), .bus_set(bus_set), .bus_enable(bus_enable),
    .bus_input(controlled_buffer_1_out), .bus_output(controlled_buffer_1_out));
  one_byte_ram one_byte_ram_241 (
    .y(decoder_1_out0), .x(decoder_2_out15), .bus_set(bus_set), .bus_enable(bus_enable),
    .bus_input(controlled_buffer_1_out), .bus_output(controlled_buffer_1_out));
  one_byte_ram one_byte_ram_242 (
    .y(decoder_1_out1), .x(decoder_2_out15), .bus_set(bus_set), .bus_enable(bus_enable),
    .bus_input(controlled_buffer_1_out), .bus_output(controlled_buffer_1_out));
  one_byte_ram one_byte_ram_243 (
    .y(decoder_1_out2), .x(decoder_2_out15), .bus_set(bus_set), .bus_enable(bus_enable),
    .bus_input(controlled_buffer_1_out), .bus_output(controlled_buffer_1_out));
  one_byte_ram one_byte_ram_244 (
    .y(decoder_1_out3), .x(decoder_2_out15), .bus_set(bus_set), .bus_enable(bus_enable),
    .bus_input(controlled_buffer_1_out), .bus_output(controlled_buffer_1_out));
  one_byte_ram one_byte_ram_245 (
    .y(decoder_1_out4), .x(decoder_2_out15), .bus_set(bus_set), .bus_enable(bus_enable),
    .bus_input(controlled_buffer_1_out), .bus_output(controlled_buffer_1_out));
  one_byte_ram one_byte_ram_246 (
    .y(decoder_1_out5), .x(decoder_2_out15), .bus_set(bus_set), .bus_enable(bus_enable),
    .bus_input(controlled_buffer_1_out), .bus_output(controlled_buffer_1_out));
  one_byte_ram one_byte_ram_247 (
    .y(decoder_1_out6), .x(decoder_2_out15), .bus_set(bus_set), .bus_enable(bus_enable),
    .bus_input(controlled_buffer_1_out), .bus_output(controlled_buffer_1_out));
  one_byte_ram one_byte_ram_248 (
    .y(decoder_1_out7), .x(decoder_2_out15), .bus_set(bus_set), .bus_enable(bus_enable),
    .bus_input(controlled_buffer_1_out), .bus_output(controlled_buffer_1_out));
  one_byte_ram one_byte_ram_249 (
    .y(decoder_1_out8), .x(decoder_2_out15), .bus_set(bus_set), .bus_enable(bus_enable),
    .bus_input(controlled_buffer_1_out), .bus_output(controlled_buffer_1_out));
  one_byte_ram one_byte_ram_250 (
    .y(decoder_1_out9), .x(decoder_2_out15), .bus_set(bus_set), .bus_enable(bus_enable),
    .bus_input(controlled_buffer_1_out), .bus_output(controlled_buffer_1_out));
  one_byte_ram one_byte_ram_251 (
    .y(decoder_1_out8), .x(decoder_2_out15), .bus_set(bus_set), .bus_enable(bus_enable),
    .bus_input(controlled_buffer_1_out), .bus_output(controlled_buffer_1_out));
  one_byte_ram one_byte_ram_252 (
    .y(decoder_1_out11), .x(decoder_2_out15), .bus_set(bus_set), .bus_enable(bus_enable),
    .bus_input(controlled_buffer_1_out), .bus_output(controlled_buffer_1_out));
  one_byte_ram one_byte_ram_253 (
    .y(decoder_1_out12), .x(decoder_2_out15), .bus_set(bus_set), .bus_enable(bus_enable),
    .bus_input(controlled_buffer_1_out), .bus_output(controlled_buffer_1_out));
  one_byte_ram one_byte_ram_254 (
    .y(decoder_1_out13), .x(decoder_2_out15), .bus_set(bus_set), .bus_enable(bus_enable),
    .bus_input(controlled_buffer_1_out), .bus_output(controlled_buffer_1_out));
  one_byte_ram one_byte_ram_255 (
    .y(decoder_1_out14), .x(decoder_2_out15), .bus_set(bus_set), .bus_enable(bus_enable),
    .bus_input(controlled_buffer_1_out), .bus_output(controlled_buffer_1_out));
  one_byte_ram one_byte_ram_256 (
    .y(decoder_1_out15), .x(decoder_2_out15), .bus_set(bus_set), .bus_enable(bus_enable),
    .bus_input(controlled_buffer_1_out), .bus_output(controlled_buffer_1_out));
  assign out_6 = bus_enable ? controlled_buffer_1_out : 8'bz;  // Controlled_Buffer controlled_buffer_2
endmodule

module Adder1 (
  input  a,
  input  b,
  input  carry_in,
  output sum,
  output co
);

  wire co1_out, co2_out, xor_1_out;

  xor xor_1 (xor_1_out, a, b);
  xor xor_2 (sum, xor_1_out, carry_in);
  and co2 (co2_out, xor_1_out, carry_in);
  and co1 (co1_out, a, b);
  or or_1 (co, co2_out, co1_out);
endmodule

module Adder8 (
  input  ci,
  input  [7:0] a,
  input  [7:0] b,
  output [7:0] o,
  output co
);

  wire adder1_1_co, adder1_2_co, adder1_3_co, adder1_4_co, adder1_5_co, adder1_6_co, adder1_7_co;

  Adder1 adder1_1 (.a(a[0]), .b(b[0]), .carry_in(ci), .sum(o[0]), .co(adder1_1_co));
  Adder1 adder1_2 (.a(a[1]), .b(b[1]), .carry_in(adder1_1_co), .sum(o[1]), .co(adder1_2_co));
  Adder1 adder1_3 (.a(a[2]), .b(b[2]), .carry_in(adder1_2_co), .sum(o[2]), .co(adder1_3_co));
  Adder1 adder1_4 (.a(a[3]), .b(b[3]), .carry_in(adder1_3_co), .sum(o[3]), .co(adder1_4_co));
  Adder1 adder1_5 (.a(a[4]), .b(b[4]), .carry_in(adder1_4_co), .sum(o[4]), .co(adder1_5_co));
  Adder1 adder1_6 (.a(a[5]), .b(b[5]), .carry_in(adder1_5_co), .sum(o[5]), .co(adder1_6_co));
  Adder1 adder1_7 (.a(a[6]), .b(b[6]), .carry_in(adder1_6_co), .sum(o[6]), .co(adder1_7_co));
  Adder1 adder1_8 (.a(a[7]), .b(b[7]), .carry_in(adder1_7_co), .sum(o[7]), .co(co));
endmodule

module SHL (
  input  shift_input,
  input  [7:0] i,
  output [7:0] o,
  output shift_output
);

  wire [6:0] eight_bit_register_1_o;

  eight_bit_register eight_bit_register_1 (.e(1'b1), .s(1'b1), .i(i), .o({shift_output, eight_bit_register_1_o}));
  eight_bit_register eight_bit_register_2 (.e(1'b1), .s(1'b1), .i({eight_bit_register_1_o, shift_input}), .o(o));

  // Notes on the sheet:
  //   start
  //   target
endmodule

module SHR (
  input  [7:0] i,
  input  shift_input,
  output shift_output,
  output [7:0] o
);

  wire [7:1] eight_bit_register_1_o;

  eight_bit_register eight_bit_register_1 (.e(1'b1), .s(1'b1), .i(i), .o({eight_bit_register_1_o, shift_output}));
  eight_bit_register eight_bit_register_2 (.e(1'b1), .s(1'b1), .i({shift_input, eight_bit_register_1_o}), .o(o));

  // Notes on the sheet:
  //   start
  //   target
endmodule

module inverter (
  input  [7:0] in_1,
  output [7:0] out_2
);

  assign out_2 = ~in_1;  // NOT_Gate not_1, 8 bits wide
endmodule

module ANDer (
  input  [7:0] a,
  input  [7:0] b,
  output [7:0] o
);

  and and_1 (o[0], a[0], b[0]);
  and and_2 (o[1], a[1], b[1]);
  and and_3 (o[2], a[2], b[2]);
  and and_4 (o[3], a[3], b[3]);
  and and_5 (o[4], a[4], b[4]);
  and and_6 (o[5], a[5], b[5]);
  and and_7 (o[6], a[6], b[6]);
  and and_8 (o[7], a[7], b[7]);
endmodule

module ORer (
  input  [7:0] a,
  input  [7:0] b,
  output [7:0] o
);

  or or_1 (o[0], a[0], b[0]);
  or or_2 (o[1], a[1], b[1]);
  or or_3 (o[2], a[2], b[2]);
  or or_4 (o[3], a[3], b[3]);
  or or_5 (o[4], a[4], b[4]);
  or or_6 (o[5], a[5], b[5]);
  or or_7 (o[6], a[6], b[6]);
  or or_8 (o[7], a[7], b[7]);
endmodule

module XOR_1 (
  input  same_input,
  input  large_input,
  input  a,
  input  b,
  output o,
  output isSame_output,
  output isLarge_output
);

  wire and_2_out, not_1_out;

  xor xor_1 (o, a, b);
  not not_1 (not_1_out, o);
  and and_1 (isSame_output, not_1_out, same_input);
  and and_2 (and_2_out, same_input, a, o);
  or or_1 (isLarge_output, and_2_out, large_input);
endmodule

module XOR_8 (
  input  [7:0] a,
  input  [7:0] b,
  output [7:0] o,
  output s_o,
  output l_o
);

  wire xor_1_1_islarge_output, xor_1_1_issame_output, xor_1_2_islarge_output, xor_1_2_issame_output,
       xor_1_3_islarge_output, xor_1_3_issame_output, xor_1_4_islarge_output, xor_1_4_issame_output,
       xor_1_5_islarge_output, xor_1_5_issame_output, xor_1_6_islarge_output, xor_1_6_issame_output,
       xor_1_7_islarge_output, xor_1_7_issame_output;

  XOR_1 xor_1_1 (
    .same_input(1'b1), .large_input(1'b0), .a(a[7]), .b(b[7]), .o(o[7]),
    .isSame_output(xor_1_1_issame_output), .isLarge_output(xor_1_1_islarge_output));
  XOR_1 xor_1_2 (
    .same_input(xor_1_1_issame_output), .large_input(xor_1_1_islarge_output), .a(a[6]), .b(b[6]), .o(o[6]),
    .isSame_output(xor_1_2_issame_output), .isLarge_output(xor_1_2_islarge_output));
  XOR_1 xor_1_3 (
    .same_input(xor_1_2_issame_output), .large_input(xor_1_2_islarge_output), .a(a[5]), .b(b[5]), .o(o[5]),
    .isSame_output(xor_1_3_issame_output), .isLarge_output(xor_1_3_islarge_output));
  XOR_1 xor_1_4 (
    .same_input(xor_1_3_issame_output), .large_input(xor_1_3_islarge_output), .a(a[4]), .b(b[4]), .o(o[4]),
    .isSame_output(xor_1_4_issame_output), .isLarge_output(xor_1_4_islarge_output));
  XOR_1 xor_1_5 (
    .same_input(xor_1_4_issame_output), .large_input(xor_1_4_islarge_output), .a(a[3]), .b(b[3]), .o(o[3]),
    .isSame_output(xor_1_5_issame_output), .isLarge_output(xor_1_5_islarge_output));
  XOR_1 xor_1_6 (
    .same_input(xor_1_5_issame_output), .large_input(xor_1_5_islarge_output), .a(a[2]), .b(b[2]), .o(o[2]),
    .isSame_output(xor_1_6_issame_output), .isLarge_output(xor_1_6_islarge_output));
  XOR_1 xor_1_7 (
    .same_input(xor_1_6_issame_output), .large_input(xor_1_6_islarge_output), .a(a[1]), .b(b[1]), .o(o[1]),
    .isSame_output(xor_1_7_issame_output), .isLarge_output(xor_1_7_islarge_output));
  XOR_1 xor_1_8 (
    .same_input(xor_1_7_issame_output), .large_input(xor_1_7_islarge_output), .a(a[0]), .b(b[0]), .o(o[0]),
    .isSame_output(s_o), .isLarge_output(l_o));
endmodule

module ZEROer (
  input  [7:0] i,
  output out_2
);

  wire or_1_out;

  or or_1 (or_1_out, i[0], i[1], i[2], i[3], i[4], i[5], i[6], i[7]);
  not not_1 (out_2, or_1_out);
endmodule

module ALU (
  input  [7:0] o,
  input  [7:0] a,
  input  [7:0] b,
  input  carry_input,
  input  [2:0] opcode,
  output a_eqaul_b,
  output a_largerthan_b,
  output zero,
  output carry_output
);

  wire adder8_1_co, and_1_out, and_2_out, and_3_out, decoder_1_out0, decoder_1_out1, decoder_1_out2,
       decoder_1_out3, decoder_1_out4, decoder_1_out5, decoder_1_out6, decoder_1_out7, shl_1_shift_output,
       shr_1_shift_output;
  wire [7:0] adder8_1_o, ander_1_o, inverter_1_out_2, orer_1_o, shl_1_o, shr_1_o, xor_8_1_o;

  XOR_8 xor_8_1 (.a(a), .b(b), .o(xor_8_1_o), .s_o(a_eqaul_b), .l_o(a_largerthan_b));
  ORer orer_1 (.a(a), .b(b), .o(orer_1_o));
  ANDer ander_1 (.a(a), .b(b), .o(ander_1_o));
  SHL shl_1 (.shift_input(carry_input), .i(a), .o(shl_1_o), .shift_output(shl_1_shift_output));
  inverter inverter_1 (.in_1(a), .out_2(inverter_1_out_2));
  SHR shr_1 (.i(a), .shift_input(carry_input), .shift_output(shr_1_shift_output), .o(shr_1_o));
  Adder8 adder8_1 (.ci(carry_input), .a(a), .b(b), .o(adder8_1_o), .co(adder8_1_co));
  Decoder #(.enable("false"), .select(3)) decoder_1 (
    .out0(decoder_1_out0), .out1(decoder_1_out1), .out2(decoder_1_out2), .out3(decoder_1_out3),
    .out4(decoder_1_out4), .out5(decoder_1_out5), .out6(decoder_1_out6), .out7(decoder_1_out7), .sel(opcode));
  and and_1 (and_1_out, shl_1_shift_output, decoder_1_out2);
  and and_2 (and_2_out, shr_1_shift_output, decoder_1_out1);
  and and_3 (and_3_out, decoder_1_out0, adder8_1_co);
  assign o = decoder_1_out7 ? {8{1'b0}} : 8'bz;  // Controlled_Buffer controlled_buffer_1
  enabler_ver2 enabler_ver2_1 (.i(xor_8_1_o), .e(decoder_1_out6), .o(o));
  enabler_ver2 enabler_ver2_2 (.i(orer_1_o), .e(decoder_1_out5), .o(o));
  enabler_ver2 enabler_ver2_3 (.i(ander_1_o), .e(decoder_1_out4), .o(o));
  enabler_ver2 enabler_ver2_4 (.i(inverter_1_out_2), .e(decoder_1_out3), .o(o));
  enabler_ver2 enabler_ver2_5 (.i(shl_1_o), .e(decoder_1_out2), .o(o));
  enabler_ver2 enabler_ver2_6 (.i(shr_1_o), .e(decoder_1_out1), .o(o));
  enabler_ver2 enabler_ver2_7 (.i(adder8_1_o), .e(decoder_1_out0), .o(o));
  or or_1 (carry_output, and_1_out, and_2_out, and_3_out);
  ZEROer zeroer_1 (.i(o), .out_2(zero));
endmodule

module CLK (
  output cIk,
  output clk_e,
  output clk_s
);

  wire clk_raw_out, j_k_ff_1_qn;

  Clock clk_raw (.out(clk_raw_out));
  J_K_Flip_Flop j_k_ff_1 (.J(1'b1), .K(1'b1), .clk(clk_raw_out), .Q(cIk), .Qn(j_k_ff_1_qn));  // open: preset, reset
  nand nand_1 (clk_e, clk_raw_out, j_k_ff_1_qn);
  and and_1 (clk_s, cIk, clk_raw_out);
endmodule

module Stepper (
  input  reset,
  input  clk,
  output step1,
  output step2,
  output step3,
  output step4,
  output step5,
  output step6,
  output step7
);

  wire not_1_out, not_2_out, not_3_out, not_4_out, not_5_out, not_6_out, not_7_out, not_8_out,
       one_bit_memory_1_o, one_bit_memory_2_o, one_bit_memory_3_o, one_bit_memory_4_o, one_bit_memory_5_o,
       one_bit_memory_6_o, one_bit_memory_7_o, one_bit_memory_8_o, one_bit_memory_9_o, one_bit_memory_10_o,
       one_bit_memory_11_o, or_1_out, or_2_out;

  not not_1 (not_1_out, clk);
  not not_2 (not_2_out, reset);
  or or_1 (or_1_out, reset, clk);
  or or_2 (or_2_out, reset, not_1_out);
  or or_3 (step1, reset, not_3_out);
  not not_3 (not_3_out, one_bit_memory_2_o);
  one_bit_memory one_bit_memory_1 (.i(not_2_out), .s(or_1_out), .o(one_bit_memory_1_o));
  one_bit_memory one_bit_memory_2 (.i(one_bit_memory_1_o), .s(or_2_out), .o(one_bit_memory_2_o));
  and and_1 (step2, one_bit_memory_2_o, not_4_out);
  one_bit_memory one_bit_memory_3 (.i(one_bit_memory_2_o), .s(or_1_out), .o(one_bit_memory_3_o));
  not not_4 (not_4_out, one_bit_memory_4_o);
  one_bit_memory one_bit_memory_4 (.i(one_bit_memory_3_o), .s(or_2_out), .o(one_bit_memory_4_o));
  one_bit_memory one_bit_memory_5 (.i(one_bit_memory_4_o), .s(or_1_out), .o(one_bit_memory_5_o));
  and and_2 (step3, one_bit_memory_4_o, not_5_out);
  not not_5 (not_5_out, one_bit_memory_6_o);
  one_bit_memory one_bit_memory_6 (.i(one_bit_memory_5_o), .s(or_2_out), .o(one_bit_memory_6_o));
  and and_3 (step4, one_bit_memory_6_o, not_6_out);
  one_bit_memory one_bit_memory_7 (.i(one_bit_memory_6_o), .s(or_1_out), .o(one_bit_memory_7_o));
  not not_6 (not_6_out, one_bit_memory_8_o);
  one_bit_memory one_bit_memory_8 (.i(one_bit_memory_7_o), .s(or_2_out), .o(one_bit_memory_8_o));
  and and_4 (step5, one_bit_memory_8_o, not_7_out);
  one_bit_memory one_bit_memory_9 (.i(one_bit_memory_8_o), .s(or_1_out), .o(one_bit_memory_9_o));
  not not_7 (not_7_out, one_bit_memory_10_o);
  one_bit_memory one_bit_memory_10 (.i(one_bit_memory_9_o), .s(or_2_out), .o(one_bit_memory_10_o));
  and and_5 (step6, one_bit_memory_10_o, not_8_out);
  one_bit_memory one_bit_memory_11 (.i(one_bit_memory_10_o), .s(or_1_out), .o(one_bit_memory_11_o));
  not not_8 (not_8_out, step7);
  one_bit_memory one_bit_memory_12 (.i(one_bit_memory_11_o), .s(or_2_out), .o(step7));
endmodule

module Stepper_ver2 (
  input  clk,
  input  reset,
  output step1,
  output step2,
  output step3,
  output step4,
  output step5,
  output step6,
  output step7
);

  wire d_ff_1_q, d_ff_2_q, d_ff_3_q, d_ff_4_q, d_ff_5_q, d_ff_6_q, d_ff_7_q, d_ff_8_q, d_ff_9_q, d_ff_10_q,
       d_ff_11_q, not_1_out, not_2_out, not_3_out, not_4_out, not_5_out, not_6_out, not_7_out, not_8_out,
       or_1_out, or_2_out;

  not not_1 (not_1_out, clk);
  not not_2 (not_2_out, step7);
  or or_1 (or_1_out, step7, clk);
  or or_2 (or_2_out, step7, not_1_out);
  D_Flip_Flop d_ff_1 (.D(not_2_out), .clk(or_1_out), .Q(d_ff_1_q), .reset(reset));  // open: Qn, preset
  or or_3 (step1, step7, not_3_out);
  not not_3 (not_3_out, d_ff_2_q);
  D_Flip_Flop d_ff_2 (.D(d_ff_1_q), .clk(or_2_out), .Q(d_ff_2_q), .reset(reset));  // open: Qn, preset
  D_Flip_Flop d_ff_3 (.D(d_ff_2_q), .clk(or_1_out), .Q(d_ff_3_q), .reset(reset));  // open: Qn, preset
  and and_1 (step2, d_ff_2_q, not_4_out);
  D_Flip_Flop d_ff_4 (.D(d_ff_3_q), .clk(or_2_out), .Q(d_ff_4_q), .reset(reset));  // open: Qn, preset
  not not_4 (not_4_out, d_ff_4_q);
  D_Flip_Flop d_ff_5 (.D(d_ff_4_q), .clk(or_1_out), .Q(d_ff_5_q), .reset(reset));  // open: Qn, preset
  and and_2 (step3, d_ff_4_q, not_5_out);
  not not_5 (not_5_out, d_ff_6_q);
  D_Flip_Flop d_ff_6 (.D(d_ff_5_q), .clk(or_2_out), .Q(d_ff_6_q), .reset(reset));  // open: Qn, preset
  D_Flip_Flop d_ff_7 (.D(d_ff_6_q), .clk(or_1_out), .Q(d_ff_7_q), .reset(reset));  // open: Qn, preset
  and and_3 (step4, d_ff_6_q, not_6_out);
  D_Flip_Flop d_ff_8 (.D(d_ff_7_q), .clk(or_2_out), .Q(d_ff_8_q), .reset(reset));  // open: Qn, preset
  not not_6 (not_6_out, d_ff_8_q);
  D_Flip_Flop d_ff_9 (.D(d_ff_8_q), .clk(or_1_out), .Q(d_ff_9_q), .reset(reset));  // open: Qn, preset
  and and_4 (step5, d_ff_8_q, not_7_out);
  not not_7 (not_7_out, d_ff_10_q);
  D_Flip_Flop d_ff_10 (.D(d_ff_9_q), .clk(or_2_out), .Q(d_ff_10_q), .reset(reset));  // open: Qn, preset
  D_Flip_Flop d_ff_11 (.D(d_ff_10_q), .clk(or_1_out), .Q(d_ff_11_q), .reset(reset));  // open: Qn, preset
  and and_5 (step6, d_ff_10_q, not_8_out);
  D_Flip_Flop d_ff_12 (.D(d_ff_11_q), .clk(or_2_out), .Q(step7), .reset(reset));  // open: Qn, preset
  not not_8 (not_8_out, step7);
endmodule

module SR_LATCH (
  input  r,
  input  s,
  output q,
  output semi_not_q
);

  nor nor_1 (q, r, semi_not_q);
  nor nor_2 (semi_not_q, q, s);
endmodule

module SR_LATCH_single_input (
  input  i,
  output q,
  output semi_not_q
);

  wire not_1_out;

  not not_1 (not_1_out, i);
  nor nor_1 (q, not_1_out, semi_not_q);
  nor nor_2 (semi_not_q, q, i);
endmodule

module SR_LATCH_enable (
  input  r,
  input  en,
  input  s,
  output q,
  output not_q
);

  wire and_1_out, and_2_out;

  and and_1 (and_1_out, r, en);
  and and_2 (and_2_out, en, s);
  nor nor_1 (q, and_1_out, not_q);
  nor nor_2 (not_q, q, and_2_out);
endmodule

module D_LATCH (
  input  en,
  input  s,
  output q,
  output not_q
);

  wire and_1_out, and_2_out, not_1_out;

  not not_1 (not_1_out, s);
  and and_1 (and_1_out, not_1_out, en);
  and and_2 (and_2_out, en, s);
  nor nor_1 (q, and_1_out, not_q);
  nor nor_2 (not_q, q, and_2_out);
endmodule

module D_flipflop (
  input  in_1,
  input  s,
  output q,
  output not_q
);

  wire and_1_out, and_2_out, and_3_out, not_1_out, not_2_out;

  not not_1 (not_1_out, in_1);
  and and_1 (and_1_out, in_1, not_1_out);
  not not_2 (not_2_out, s);
  and and_2 (and_2_out, not_2_out, and_1_out);
  and and_3 (and_3_out, and_1_out, s);
  nor nor_1 (q, and_2_out, not_q);
  nor nor_2 (not_q, q, and_3_out);
endmodule

module Control_Unit (
  input  IR_0,
  input  IR_1,
  input  IR_2,
  input  IR_3,
  input  IR_4,
  input  IR_5,
  input  IR_6,
  input  IR_7,
  output R0_E,
  output IR_S,
  output MAR_S,
  output R1_E,
  output IAR_S,
  output R2_E,
  output RAM_S,
  output TMP_S,
  output R3_E,
  output ACC_S,
  output ACC_E,
  output R0_S,
  output RAM_E,
  output R1_S,
  output R2_S,
  output IAR_E,
  output R3_S,
  output BUS1_E
);

  wire clk_1_cik, clk_1_clk_e, clk_1_clk_s, stepper_ver2_1_step2, stepper_ver2_1_step3, stepper_ver2_1_step4,
       stepper_ver2_1_step5, stepper_ver2_1_step6, stepper_ver2_1_step7;

  // AND_Gate and_1 has open pins: out=R0_E
  // AND_Gate and_2 has open pins: out=R1_E
  // AND_Gate and_3 has open pins: out=R2_E
  // AND_Gate and_4 has open pins: out=R3_E
  and and_5 (ACC_E, clk_1_clk_e, stepper_ver2_1_step3);
  and and_6 (RAM_E, clk_1_clk_e, stepper_ver2_1_step2);
  and and_7 (IAR_E, clk_1_clk_e, BUS1_E);
  CLK clk_1 (.cIk(clk_1_cik), .clk_e(clk_1_clk_e), .clk_s(clk_1_clk_s));
  Stepper_ver2 stepper_ver2_1 (
    .clk(clk_1_cik), .reset(stepper_ver2_1_step7), .step1(BUS1_E), .step2(stepper_ver2_1_step2),
    .step3(stepper_ver2_1_step3), .step4(stepper_ver2_1_step4), .step5(stepper_ver2_1_step5),
    .step6(stepper_ver2_1_step6), .step7(stepper_ver2_1_step7));
  and and_8 (IR_S, clk_1_clk_s, stepper_ver2_1_step2);
  and and_9 (MAR_S, clk_1_clk_s, BUS1_E);
  and and_10 (IAR_S, clk_1_clk_s, stepper_ver2_1_step3);
  // AND_Gate and_11 has open pins: out=RAM_S
  // AND_Gate and_12 has open pins: out=TMP_S
  buf and_13 (ACC_S, BUS1_E);  // AND_Gate
  // AND_Gate and_14 has open pins: out=R0_S
  // AND_Gate and_15 has open pins: out=R1_S
  // AND_Gate and_16 has open pins: out=R2_S
  // AND_Gate and_17 has open pins: out=R3_S

  // Notes on the sheet:
  //   IR_in
endmodule

module CPU (
);

  wire undriven, undriven_3, undriven_4, undriven_5, undriven_6, undriven_7, undriven_8, undriven_9,
       undriven_10, undriven_11, undriven_12;
  wire [7:0] ACC_o, bus1_1_o, TMP_o, undriven_2;

  eight_bit_register TMP (.e(1'b1), .s(undriven), .i(ACC_o), .o(TMP_o));
  ALU alu_1 (
    .o(undriven_2), .a(ACC_o), .b(bus1_1_o));  // open: carry_input, opcode, a_eqaul_b, a_largerthan_b, zero, carry_output
  eight_bit_register ACC (.e(undriven_4), .s(undriven_3), .i(undriven_2), .o(ACC_o));
  BUS1 bus1_1 (.i(TMP_o), .o(bus1_1_o));  // open: bus1_e
  eight_bit_register R0 (.e(undriven_5), .s(undriven_6), .i(ACC_o), .o(ACC_o));
  eight_bit_register IAR ();  // open: e, s, i, o
  eight_bit_register R1 (.e(undriven_8), .s(undriven_7), .i(ACC_o), .o(ACC_o));
  Control_Unit control_unit_1 ();  // open: IR_0, IR_1, IR_2, IR_3, IR_4, IR_5, IR_6, IR_7, R0_E, IR_S, MAR_S, R1_E, IAR_S, R2_E, RAM_S, TMP_S, R3_E, ACC_S, ACC_E, R0_S, RAM_E, R1_S, R2_S, IAR_E, R3_S, BUS1_E
  eight_bit_register R2 (.e(undriven_9), .s(undriven_10), .i(ACC_o), .o(ACC_o));
  IR ir_1 ();  // open: s, i, o0, o1, o2, o3, o4, o5, o6, o7
  eight_bit_register R3 (.e(undriven_11), .s(undriven_12), .i(ACC_o), .o(ACC_o));
endmodule

module BUS1 (
  input  [7:0] i,
  input  bus1_e,
  output [7:0] o
);

  wire not_1_out;

  not not_1 (not_1_out, bus1_e);
  assign o = not_1_out ? i : 8'bz;  // Controlled_Buffer controlled_buffer_1
  assign o = bus1_e ? 8'h1 : 8'bz;  // Controlled_Buffer controlled_buffer_2
endmodule

module IR (
  input  s,
  input  [7:0] i,
  output o0,
  output o1,
  output o2,
  output o3,
  output o4,
  output o5,
  output o6,
  output o7
);

  wire [7:0] controlled_buffer_1_out;

  assign controlled_buffer_1_out = s ? i : 8'bz;  // Controlled_Buffer controlled_buffer_1
  eight_bit_memory eight_bit_memory_1 (.s(s), .i(controlled_buffer_1_out), .o({o7, o6, o5, o4, o3, o2, o1, o0}));
endmodule
